// Logisim project CUP.circ as structural Verilog: 1 circuit, main circuit main
module main (
  output [23:0] RegData1,
  output [23:0] ReadData2
);

  wire and_1_out, and_2_out, and_3_out, and_4_out, and_5_out, and_6_out, clock_1_out, decoder_1_out0,
       decoder_1_out1, decoder_1_out2, decoder_1_out3, decoder_1_out4;
  wire [2:0] ram_1_dout_3, ram_1_dout_5;
  wire [7:0] adder_1_out, PC_q;
  wire [15:0] ram_1_dout_4;
  wire [23:0] adder_2_out, demultiplexer_1_out1, demultiplexer_1_out2, demultiplexer_1_out3,
       demultiplexer_2_out1, demultiplexer_2_out2, multiplexer_3_out, multiplier_1_out, ram_1_dout,
       ram_1_dout_2, ram_2_dout, X0_q, X1_q, X2_q, X3_q, X31_q;
  wire [63:0] undriven;

  Decoder #(.select(3)) decoder_1 (
    .out0(decoder_1_out0), .out1(decoder_1_out1), .out2(decoder_1_out2), .out3(decoder_1_out3),
    .out4(decoder_1_out4), .sel(ram_1_dout_4[14:12]));  // open: out5, out6, out7, en
  and and_1 (and_1_out, 1'b1, decoder_1_out0);
  and and_2 (and_2_out, 1'b1, decoder_1_out1);
  and and_3 (and_3_out, 1'b1, decoder_1_out2);
  and and_4 (and_4_out, 1'b1, decoder_1_out3);
  and and_5 (and_5_out, 1'b1, decoder_1_out4);
  Register PC (.D(adder_1_out), .en(1'b1), .clk(clock_1_out), .Q(PC_q));  // open: clr
  Adder adder_1 (.a(8'h1), .b(PC_q), .out(adder_1_out));  // open: cin, cout
  Clock clock_1 (.out(clock_1_out));
  Register #(.width(24)) X31 (.D(multiplexer_3_out), .en(and_1_out), .clk(clock_1_out), .Q(X31_q));  // open: clr
  Register #(.width(24)) X0 (.D(multiplexer_3_out), .en(and_2_out), .clk(clock_1_out), .Q(X0_q));  // open: clr
  Register #(.width(24)) X1 (.D(multiplexer_3_out), .en(and_3_out), .clk(clock_1_out), .Q(X1_q));  // open: clr
  Register #(.width(24)) X2 (.D(multiplexer_3_out), .en(and_4_out), .clk(clock_1_out), .Q(X2_q));  // open: clr
  Register #(.width(24)) X3 (.D(multiplexer_3_out), .en(and_5_out), .clk(clock_1_out), .Q(X3_q));  // open: clr
  RAM #(.dataWidth(64)) ram_1 (
    .addr(PC_q), .we(1'b0), .oe(1'b1), .clk(clock_1_out), .din(undriven),
    .dout({ram_1_dout_2, ram_1_dout, ram_1_dout_4[15:11], ram_1_dout_3, ram_1_dout_4[7], ram_1_dout_5, ram_1_dout_4[3:0]}));
  Multiplexer #(.select(3), .width(24)) multiplexer_1 (
    .in0(X31_q), .in1(X0_q), .in2(X1_q), .in3(X2_q), .in4(X3_q), .in5(ram_1_dout), .in6(ram_1_dout_2),
    .out(RegData1), .sel(ram_1_dout_5));  // open: in7
  Multiplexer #(.select(3), .width(24)) multiplexer_2 (
    .in0(X31_q), .in1(X0_q), .in2(X1_q), .in3(X2_q), .in4(X3_q), .in5(ram_1_dout), .in6(ram_1_dout_2),
    .out(ReadData2), .sel(ram_1_dout_3));  // open: in7
  and and_6 (and_6_out, ram_1_dout_4[1], ram_1_dout_4[0]);
  Demultiplexer #(.select(3), .width(24)) demultiplexer_1 (
    .out1(demultiplexer_1_out1), .out2(demultiplexer_1_out2), .out3(demultiplexer_1_out3), .in(RegData1),
    .sel(ram_1_dout_4[2:0]));  // open: out0, out4, out5, out6, out7
  Demultiplexer #(.select(3), .width(24)) demultiplexer_2 (
    .out1(demultiplexer_2_out1), .out2(demultiplexer_2_out2), .in(ReadData2), .sel(ram_1_dout_4[2:0]));  // open: out0, out3, out4, out5, out6, out7
  Adder #(.width(24)) adder_2 (
    .a(demultiplexer_1_out1), .b(demultiplexer_2_out1), .out(adder_2_out));  // open: cin, cout
  Multiplier #(.width(24)) multiplier_1 (
    .a(demultiplexer_1_out2), .b(demultiplexer_2_out2), .out(multiplier_1_out));  // open: cin, cout
  RAM #(.addrWidth(3), .dataWidth(24)) ram_2 (
    .addr(ram_1_dout_4[14:12]), .we(and_6_out), .oe(1'b1), .clk(clock_1_out), .din(demultiplexer_1_out3),
    .dout(ram_2_dout));
  Multiplexer #(.select(3), .width(24)) multiplexer_3 (
    .in0({24{1'b0}}), .in1(adder_2_out), .in2(multiplier_1_out), .in3(demultiplexer_1_out3),
    .in4(ram_2_dout), .out(multiplexer_3_out), .sel(ram_1_dout_4[2:0]));  // open: in5, in6, in7

  // Notes on the sheet:
  //   RegWrite
  //   Write Reg
  //   Register File
  //   RegDataW
  //   Instruction Memory
  //   operation
  //   Rn
  //   Rm
  //   second imediate value
  //   Rd
  //   first imediate value 
  //   Adib Osmany & Neel Meyyur
  //   I pledge my honor that I have abided by the Stevens Honor System.
  //   Name of CPU: CUP
  //   "ALU"
  //   helps to determine which operation to use
  //   port1: add
  //   port2: mult
  //   port3: str
  //   port4: ldr
  //   DATA MEMORY
  //   port 0: empty port (base case)
endmodule
